// Logisim project Elevator.circ as structural Verilog: 7 circuits, main circuit main
module main (
);

  wire _0_2_out, _1_2_out, _2_2_out, _3_2_out, and_1_out, and_2_out, and_3_out, clock_1_out, clock_2_out,
       comparateur_1_out_5, comparateur_1_out_6, comparateur_1_out_7, counter_1_o1, counter_1_o2, d_ff_1_q,
       d_ff_2_q, d_ff_3_q, encoder_1_b0, encoder_1_b1, lifting_machine_2_0_1_out_4, lifting_machine_2_0_1_s2,
       not_1_out, not_2_out, O1_q, O1_qn, O2_q, O2_qn, or_1_out, or_2_out, triger_1__0_2, triger_1__1_2,
       triger_1__2_2, triger_1__3_2, xnor_1_out;

  LED _0 (.in(triger_1__0_2));
  Button _0_2 (.out(_0_2_out));
  LED _1 (.in(triger_1__1_2));
  Button _1_2 (.out(_1_2_out));
  LED _2 (.in(triger_1__2_2));
  Button _2_2 (.out(_2_2_out));
  LED _3 (.in(triger_1__3_2));
  Button _3_2 (.out(_3_2_out));
  Clock clock_1 (.out(clock_1_out));
  Triger triger_1 (
    ._0(_0_2_out), ._1(_1_2_out), ._2(_2_2_out), ._3(_3_2_out), .clk(clock_1_out), ._0_2(triger_1__0_2),
    ._1_2(triger_1__1_2), ._2_2(triger_1__2_2), ._3_2(triger_1__3_2));
  Encoder encoder_1 (
    ._0(triger_1__0_2), ._1(triger_1__1_2), ._2(triger_1__2_2), ._3(triger_1__3_2), .B1(encoder_1_b1),
    .B0(encoder_1_b0));
  Clock #(.highDuration(150), .lowDuration(150)) clock_2 (.out(clock_2_out));
  Comparateur comparateur_1 (
    .B1(encoder_1_b1), .B0(encoder_1_b0), .O1(O1_q), .O2(O2_q), .out_5(comparateur_1_out_5),
    .out_6(comparateur_1_out_6), .out_7(comparateur_1_out_7));
  Counter counter_1 (
    .i0(comparateur_1_out_5), .i1(comparateur_1_out_6), .i2(comparateur_1_out_7), .CLK(clock_2_out),
    .O1(counter_1_o1), .O2(counter_1_o2));
  or or_1 (or_1_out, O1_q, O2_qn);
  D_Flip_Flop O1 (.clk(clock_2_out), .D(counter_1_o1), .Q(O1_q), .Qn(O1_qn));  // open: preset, en, reset
  Lifting_Machine_2_0 lifting_machine_2_0_1 (
    .i0(comparateur_1_out_5), .i1(comparateur_1_out_6), .i2(comparateur_1_out_7),
    .out_4(lifting_machine_2_0_1_out_4), .S2(lifting_machine_2_0_1_s2));
  and and_1 (and_1_out, O1_qn, O2_qn);
  D_Flip_Flop O2 (.clk(clock_2_out), .D(counter_1_o2), .Q(O2_q), .Qn(O2_qn));  // open: preset, en, reset
  _7_Segment_Display u_7_segment_display_1 (
    .g(O1_q), .f(and_1_out), .a(or_1_out), .b(1'b1), .e(O2_qn), .d(or_1_out), .c(or_2_out));  // open: dp
  or or_2 (or_2_out, O2_q, O1_qn);
  xnor xnor_1 (xnor_1_out, lifting_machine_2_0_1_out_4, lifting_machine_2_0_1_s2);
  not not_1 (not_1_out, lifting_machine_2_0_1_out_4);
  not not_2 (not_2_out, lifting_machine_2_0_1_s2);
  D_Flip_Flop d_ff_1 (.clk(clock_2_out), .D(xnor_1_out), .Q(d_ff_1_q));  // open: Qn, preset, en, reset
  D_Flip_Flop d_ff_2 (.clk(clock_2_out), .D(and_2_out), .Q(d_ff_2_q));  // open: Qn, preset, en, reset
  and and_2 (and_2_out, not_1_out, lifting_machine_2_0_1_s2);
  and and_3 (and_3_out, not_2_out, lifting_machine_2_0_1_out_4);
  D_Flip_Flop d_ff_3 (.clk(clock_2_out), .D(and_3_out), .Q(d_ff_3_q));  // open: Qn, preset, en, reset
  LED led_1 (.in(d_ff_1_q));
  LED led_2 (.in(d_ff_2_q));
  LED led_3 (.in(d_ff_3_q));

  // Notes on the sheet:
  //   a
  //   f
  //   e
  //   d
  //   g
  //   c
  //   b
  //   MoveDown
  //   Stop!
  //   MoveUP
endmodule

module Encoder (
  input  _0,
  input  _1,
  input  _2,
  input  _3,
  output B1,
  output B0
);

  wire and_1_out, not_1_out, or_1_out;

  not not_1 (not_1_out, _2);
  or or_1 (or_1_out, _0, _2, _3, _2);
  and and_1 (and_1_out, _1, not_1_out);
  or or_2 (B0, and_1_out, _3);
  or or_3 (B1, _2, _3);
endmodule

// Comp
module Comparateur (
  input  B1,
  input  B0,
  input  O1,
  input  O2,
  output out_5,
  output out_6,
  output out_7
);

  wire and_1_out, and_2_out, and_3_out, and_4_out, and_5_out, and_6_out, and_7_out, not_1_out, not_2_out,
       not_3_out, not_4_out, or_1_out, or_2_out, xnor_1_out, xnor_2_out;

  not not_1 (not_1_out, O1);
  not not_2 (not_2_out, O2);
  not not_3 (not_3_out, B1);
  not not_4 (not_4_out, B0);
  and and_1 (and_1_out, B0, not_2_out);
  xnor xnor_1 (xnor_1_out, B1, O1);
  and and_2 (and_2_out, not_3_out, O1);
  and and_3 (and_3_out, not_4_out, O2);
  and and_4 (and_4_out, B1, not_1_out);
  and and_5 (and_5_out, and_1_out, xnor_1_out);
  and and_6 (and_6_out, xnor_1_out, and_3_out);
  or or_1 (or_1_out, and_4_out, and_5_out);
  and and_7 (and_7_out, xnor_1_out, xnor_2_out);
  xnor xnor_2 (xnor_2_out, B0, O2);
  or or_2 (or_2_out, and_2_out, and_6_out);
  and and_8 (out_5, or_1_out, or_1_out);
  and and_9 (out_6, and_7_out, and_7_out);
  and and_10 (out_7, or_2_out, or_2_out);

  // Notes on the sheet:
  //   B0*O2'
endmodule

// count
module Counter (
  input  i0,
  input  i1,
  input  i2,
  input  CLK,
  output O1,
  output O2
);

  wire and_1_out, and_2_out, and_3_out, and_4_out, and_5_out, and_6_out, and_7_out, and_8_out, and_9_out,
       and_10_out, and_11_out, and_12_out, and_13_out, c0_q, c0_qn, c1_q, c1_qn, not_1_out, not_2_out,
       not_3_out, not_4_out, not_5_out, not_6_out, not_7_out, not_8_out, not_9_out, not_10_out, not_11_out,
       not_12_out, or_1_out, or_2_out;

  not not_1 (not_1_out, i0);
  not not_2 (not_2_out, i1);
  not not_3 (not_3_out, i2);
  and and_1 (and_1_out, not_2_out, not_3_out, i0, c1_q);
  and and_2 (and_2_out, not_1_out, not_2_out, i2, c1_qn);
  not not_4 (not_4_out, i1);
  not not_5 (not_5_out, i2);
  not not_6 (not_6_out, i0);
  not not_7 (not_7_out, i1);
  not not_8 (not_8_out, i0);
  and and_3 (and_3_out, not_8_out, not_4_out, i2);
  and and_4 (and_4_out, not_4_out, not_5_out, i0);
  or or_1 (or_1_out, and_1_out, and_2_out);
  not not_9 (not_9_out, i2);
  or or_2 (or_2_out, and_3_out, and_4_out);
  T_Flip_Flop c0 (.clk(CLK), .T(or_1_out), .Q(c0_q), .Qn(c0_qn));  // open: preset, reset, en
  T_Flip_Flop c1 (.clk(CLK), .T(or_2_out), .Q(c1_q), .Qn(c1_qn));  // open: preset, reset, en
  not not_10 (not_10_out, i0);
  not not_11 (not_11_out, i1);
  not not_12 (not_12_out, i2);
  and and_5 (and_5_out, not_6_out, not_7_out, i2, c0_qn, c1_qn);
  and and_6 (and_6_out, i0, not_7_out, not_9_out, c1_q, c0_qn);
  and and_7 (and_7_out, not_6_out, not_7_out, c1_q, c0_q);
  and and_8 (and_8_out, not_7_out, not_9_out, c0_q, c1_qn);
  and and_9 (and_9_out, not_8_out, i1, not_9_out, c0_q);
  or or_3 (O1, and_5_out, and_6_out, and_7_out, and_8_out, and_9_out);
  and and_10 (and_10_out, not_10_out, not_11_out, not_12_out, c1_q);
  and and_11 (and_11_out, not_10_out, not_11_out, i2, c1_qn);
  and and_12 (and_12_out, not_10_out, i1, not_12_out, c1_q);
  and and_13 (and_13_out, i0, not_11_out, not_12_out, c1_qn);
  or or_4 (O2, and_10_out, and_11_out, and_12_out, and_13_out);

  // Notes on the sheet:
  //   i0
  //   i1
  //   i2
endmodule

module Triger (
  input  _0,
  input  _1,
  input  _2,
  input  _3,
  input  clk,
  output _0_2,
  output _1_2,
  output _2_2,
  output _3_2
);

  wire or_1_out, or_2_out, or_3_out, or_4_out;

  or or_1 (or_1_out, _1, _2, _3);
  or or_2 (or_2_out, _0, _2, _3);
  or or_3 (or_3_out, _0, _1, _3);
  J_K_Flip_Flop j_k_ff_1 (.J(_0), .clk(clk), .K(or_1_out), .Q(_0_2));  // open: Qn, preset, en, reset
  J_K_Flip_Flop j_k_ff_2 (.J(_1), .clk(clk), .K(or_2_out), .Q(_1_2));  // open: Qn, preset, en, reset
  J_K_Flip_Flop j_k_ff_3 (.J(_2), .clk(clk), .K(or_3_out), .Q(_2_2));  // open: Qn, preset, en, reset
  J_K_Flip_Flop j_k_ff_4 (.J(_3), .clk(clk), .K(or_4_out), .Q(_3_2));  // open: Qn, preset, en, reset
  or or_4 (or_4_out, _0, _2, _1);
endmodule

// lift
module LiftingMachine (
  input  i0,
  input  i1,
  input  i2,
  input  Clock,
  output O_prime_1,
  output O_prime_2
);

  wire and_1_out, and_2_out, and_3_out, and_4_out, and_5_out, and_6_out, and_7_out, and_8_out, and_9_out,
       and_10_out, and_11_out, and_12_out, and_13_out, and_14_out, and_15_out, and_16_out, and_17_out,
       and_18_out, and_19_out, and_20_out, Jk1_q, Jk1_qn, Jk2_q, Jk2_qn, not_1_out, not_2_out, not_3_out,
       not_4_out, not_5_out, not_6_out, not_7_out, not_8_out, not_9_out, or_1_out, or_2_out;

  not not_1 (not_1_out, i0);
  not not_2 (not_2_out, i1);
  not not_3 (not_3_out, i2);
  not not_4 (not_4_out, Jk1_q);
  not not_5 (not_5_out, Jk2_q);
  and and_1 (and_1_out, not_1_out, not_2_out, not_3_out, not_4_out);
  and and_2 (and_2_out, not_1_out, not_2_out, Jk2_q, not_1_out);
  and and_3 (and_3_out, not_2_out, not_3_out, Jk1_q);
  and and_4 (and_4_out, not_1_out, i1, not_3_out);
  and and_5 (and_5_out, not_2_out, not_3_out, Jk1_q);
  and and_6 (and_6_out, Jk1_q, not_2_out, Jk2_q, Jk1_q);
  and and_7 (and_7_out, not_2_out, not_3_out, not_5_out, i0);
  and and_8 (and_8_out, i0, Jk1_q, not_2_out, not_3_out);
  and and_9 (and_9_out, not_2_out, not_3_out, not_5_out, Jk1_q);
  and and_10 (and_10_out, Jk2_q, not_2_out, not_1_out);
  and and_11 (and_11_out, i2, i1, not_1_out);
  or or_1 (or_1_out, and_1_out, and_2_out, and_3_out, and_4_out, and_5_out);
  and and_12 (and_12_out, not_2_out, not_3_out, i0, Jk1_q, Jk2_q);
  and and_13 (and_13_out, and_6_out, not_1_out);
  or or_2 (or_2_out, and_7_out, and_8_out, and_9_out, and_10_out, and_11_out);
  J_K_Flip_Flop Jk1 (.J(or_1_out), .clk(Clock), .K(and_12_out), .Q(Jk1_q), .Qn(Jk1_qn));  // open: preset, en, reset
  not not_6 (not_6_out, i0);
  not not_7 (not_7_out, i1);
  not not_8 (not_8_out, i2);
  not not_9 (not_9_out, Jk1_q);
  J_K_Flip_Flop Jk2 (.J(or_2_out), .clk(Clock), .K(and_13_out), .Q(Jk2_q), .Qn(Jk2_qn));  // open: preset, en, reset
  and and_14 (and_14_out, Jk2_q, not_6_out, not_7_out);
  and and_15 (and_15_out, not_7_out, not_6_out, i2, Jk1_qn);
  and and_16 (and_16_out, not_6_out, not_7_out, i2);
  and and_17 (and_17_out, not_7_out, not_8_out, Jk1_q, Jk2_qn);
  and and_18 (and_18_out, Jk1_q, not_8_out, not_7_out);
  and and_19 (and_19_out, not_8_out, i1, not_6_out);
  and and_20 (and_20_out, not_8_out, not_7_out, i0, Jk2_qn);
  or or_3 (O_prime_2, and_18_out, and_19_out, and_20_out);
  or or_4 (O_prime_1, and_14_out, and_15_out, and_16_out, and_17_out);
endmodule

// Lift
module Lifting_Machine_2_0 (
  input  i0,
  input  i1,
  input  i2,
  output out_4,
  output S2
);

  wire and_1_out, and_2_out, and_3_out, not_1_out, not_2_out, not_3_out;

  not not_1 (not_1_out, i0);
  not not_2 (not_2_out, i1);
  not not_3 (not_3_out, i2);
  and and_1 (and_1_out, not_3_out, not_2_out);
  and and_2 (and_2_out, not_1_out, not_2_out);
  and and_3 (and_3_out, not_1_out, not_3_out);
  or or_1 (out_4, and_2_out, and_3_out);
  or or_2 (S2, and_3_out, and_1_out);
endmodule
