// Logisim project TrafficLight.circ as structural Verilog: 2 circuits, main circuit main
module main (
);

  wire clock_1_out, traffic_light_signal_producer_1_green, traffic_light_signal_producer_1_green_2,
       traffic_light_signal_producer_1_red, traffic_light_signal_producer_1_red_2,
       traffic_light_signal_producer_1_yellow, traffic_light_signal_producer_1_yellow_2;

  Clock #(.highDuration(30), .lowDuration(30)) clock_1 (.out(clock_1_out));
  Traffic_light_signal_producer traffic_light_signal_producer_1 (
    .Green(traffic_light_signal_producer_1_green), .Yellow(traffic_light_signal_producer_1_yellow),
    .Red(traffic_light_signal_producer_1_red), .Green_2(traffic_light_signal_producer_1_green_2),
    .Yellow_2(traffic_light_signal_producer_1_yellow_2), .Red_2(traffic_light_signal_producer_1_red_2),
    .Clk(clock_1_out));
  LED led_1 (.in(traffic_light_signal_producer_1_green));
  LED led_2 (.in(traffic_light_signal_producer_1_yellow));
  LED led_3 (.in(traffic_light_signal_producer_1_red));
  LED led_4 (.in(traffic_light_signal_producer_1_green_2));
  LED led_5 (.in(traffic_light_signal_producer_1_yellow_2));
  LED led_6 (.in(traffic_light_signal_producer_1_red_2));
  LED led_7 (.in(traffic_light_signal_producer_1_green));
  LED led_8 (.in(traffic_light_signal_producer_1_yellow));
  LED led_9 (.in(traffic_light_signal_producer_1_red));
  LED led_10 (.in(traffic_light_signal_producer_1_green_2));
  LED led_11 (.in(traffic_light_signal_producer_1_yellow_2));
  LED led_12 (.in(traffic_light_signal_producer_1_red_2));

  // Notes on the sheet:
  //   street1
  //   street 3
  //   street2
  //   street4
endmodule

module Traffic_light_signal_producer (
  input  Clk,
  output Green,
  output Yellow,
  output Red,
  output Green_2,
  output Yellow_2,
  output Red_2
);

  wire and_1_out, and_2_out, and_3_out, and_4_out, not_1_out, not_2_out, not_3_out, not_4_out, not_5_out,
       not_6_out, or_1_out, or_2_out, or_3_out, or_4_out, Q0_q, Q0_qn, Q1_q, Q1_qn, Q2_q, Q2_qn, Q3_q, Q3_qn;

  and and_1 (and_1_out, Q0_qn, Q2_qn, Q3_q);
  T_Flip_Flop #(.trigger("falling")) Q0 (.clk(Clk), .T(1'b1), .Q(Q0_q), .Qn(Q0_qn));  // open: preset, reset, en
  or or_1 (or_1_out, and_1_out, and_2_out);
  and and_2 (and_2_out, Q1_qn, Q2_qn, Q3_q);
  T_Flip_Flop #(.trigger("falling")) Q1 (.clk(Q0_q), .T(1'b1), .Q(Q1_q), .Qn(Q1_qn));  // open: preset, reset, en
  and and_3 (and_3_out, Q0_qn, Q2_qn, Q3_qn);
  or or_2 (or_2_out, and_3_out, and_4_out);
  and and_4 (and_4_out, Q1_qn, Q2_qn, Q3_qn);
  or or_3 (or_3_out, or_1_out, Q3_qn);
  T_Flip_Flop #(.trigger("falling")) Q2 (.clk(Q1_q), .T(1'b1), .Q(Q2_q), .Qn(Q2_qn));  // open: preset, reset, en
  not not_1 (not_1_out, or_1_out);
  T_Flip_Flop #(.trigger("falling")) Q3 (.clk(Q2_q), .T(1'b1), .Q(Q3_q), .Qn(Q3_qn));  // open: preset, reset, en
  or or_4 (or_4_out, or_2_out, Q3_q);
  not not_2 (not_2_out, or_4_out);
  not not_3 (not_3_out, or_2_out);
  not not_4 (not_4_out, or_2_out);
  not not_5 (not_5_out, or_1_out);
  not not_6 (not_6_out, or_3_out);
  and and_5 (Green_2, not_2_out, not_3_out);
  and and_6 (Yellow_2, or_4_out, or_2_out);
  and and_7 (Red_2, not_4_out, or_4_out);
  and and_8 (Green, not_5_out, not_6_out);
  and and_9 (Yellow, or_1_out, or_3_out);
  and and_10 (Red, not_1_out, or_3_out);

  // Notes on the sheet:
  //   s0
  //   s0"
  //   s1
  //   s1"
endmodule
